// Logisim project 8Bit-Ripple-Carry.circ as structural Verilog: 1 circuit, main circuit main
module main (
  input  A0,
  input  A1,
  input  A2,
  input  A3,
  input  A4,
  input  A5,
  input  A6,
  input  A7,
  input  B0,
  input  B1,
  input  B2,
  input  B3,
  input  B4,
  input  B5,
  input  B6,
  input  B7,
  input  C_input,
  output Sum0,
  output Sum1,
  output Sum2,
  output Sum3,
  output Sum4,
  output Sum5,
  output Sum6,
  output Sum7
);

  wire AND_2_out, AND_3_out, AND_4_out, AND_5_out, AND_6_out, AND_7_out, AND_8_out, AND_9_out, AND_10_out,
       AND_11_out, AND_12_out, AND_13_out, AND_14_out, AND_15_out, AND_16_out, AND_out, OR_2_out, OR_3_out,
       OR_4_out, OR_5_out, OR_6_out, OR_7_out, OR_8_out, OR_out, XOR_3_out, XOR_5_out, XOR_7_out, XOR_9_out,
       XOR_11_out, XOR_13_out, XOR_15_out, XOR_out;

  xor XOR (XOR_out, A0, B0);
  and AND (AND_out, A0, A0, B0);
  xor XOR_2 (Sum0, XOR_out, C_input);
  and AND_2 (AND_2_out, XOR_out, C_input);
  or OR (OR_out, AND_2_out, AND_out);
  xor XOR_3 (XOR_3_out, A1, B1);
  and AND_3 (AND_3_out, A1, A1, B1);
  xor XOR_4 (Sum1, XOR_3_out, OR_out);
  and AND_4 (AND_4_out, XOR_3_out, OR_out);
  or OR_2 (OR_2_out, AND_4_out, AND_3_out);
  xor XOR_5 (XOR_5_out, A2, B2);
  and AND_5 (AND_5_out, A2, A2, B2);
  xor XOR_6 (Sum2, XOR_5_out, OR_2_out);
  and AND_6 (AND_6_out, XOR_5_out, OR_2_out);
  or OR_3 (OR_3_out, AND_6_out, AND_5_out);
  xor XOR_7 (XOR_7_out, A3, B3);
  and AND_7 (AND_7_out, A3, A3, B3);
  xor XOR_8 (Sum3, XOR_7_out, OR_3_out);
  and AND_8 (AND_8_out, XOR_7_out, OR_3_out);
  or OR_4 (OR_4_out, AND_8_out, AND_7_out);
  xor XOR_9 (XOR_9_out, A4, B4);
  and AND_9 (AND_9_out, A4, A4, B4);
  xor XOR_10 (Sum4, XOR_9_out, OR_4_out);
  and AND_10 (AND_10_out, XOR_9_out, OR_4_out);
  or OR_5 (OR_5_out, AND_10_out, AND_9_out);
  xor XOR_11 (XOR_11_out, A5, B5);
  and AND_11 (AND_11_out, A5, A5, B5);
  xor XOR_12 (Sum5, XOR_11_out, OR_5_out);
  and AND_12 (AND_12_out, XOR_11_out, OR_5_out);
  or OR_6 (OR_6_out, AND_12_out, AND_11_out);
  xor XOR_13 (XOR_13_out, A6, B6);
  and AND_13 (AND_13_out, A6, A6, B6);
  xor XOR_14 (Sum6, XOR_13_out, OR_6_out);
  and AND_14 (AND_14_out, XOR_13_out, OR_6_out);
  or OR_7 (OR_7_out, AND_14_out, AND_13_out);
  xor XOR_15 (XOR_15_out, A7, B7);
  and AND_15 (AND_15_out, A7, A7, B7);
  xor XOR_16 (Sum7, XOR_15_out, OR_7_out);
  and AND_16 (AND_16_out, XOR_15_out, OR_7_out);
  or OR_8 (OR_8_out, AND_16_out, AND_15_out);
endmodule
