// Logisim project Full-adder.circ as structural Verilog: 1 circuit, main circuit main
module main (
  input  A,
  input  B,
  input  C_input,
  output Sum,
  output C_output
);

  wire AND_2_out, AND_out, XOR_out;

  xor XOR (XOR_out, A, B);
  and AND (AND_out, A, A, B);
  xor XOR_2 (Sum, XOR_out, C_input);
  and AND_2 (AND_2_out, XOR_out, C_input);
  or OR (C_output, AND_2_out, AND_out);
endmodule
