// Logisim project half-adder.circ as structural Verilog: 1 circuit, main circuit main
module main (
  input  A,
  input  B,
  output out_3,
  output out_4
);

  xor XOR (out_3, A, B);
  and AND (out_4, B, A);
endmodule
