// Logisim project 2x multiplexer.circ as structural Verilog: 1 circuit, main circuit main
module main (
  input  Input0,
  input  Input1,
  input  Select0,
  output Output0
);

  wire and_1_out, and_2_out, not_1_out;

  not not_1 (not_1_out, Select0);
  and and_1 (and_1_out, Input0, not_1_out);
  and and_2 (and_2_out, Input1, Select0);
  or or_1 (Output0, and_1_out, and_2_out);
endmodule
