// Logisim project 4X-Multiplexer.circ as structural Verilog: 1 circuit, main circuit main
module main (
  input  Input0,
  input  Input1,
  input  Input2,
  input  Input3,
  input  S0,
  input  S1,
  output Output0,
  output Output1
);

  wire and_1_out, and_2_out, and_3_out, and_4_out, not_1_out, not_2_out;

  not not_1 (not_1_out, S1);
  not not_2 (not_2_out, S0);
  and and_1 (and_1_out, Input0, S0);
  and and_2 (and_2_out, Input1, not_2_out);
  and and_3 (and_3_out, Input2, S1);
  and and_4 (and_4_out, Input3, not_1_out);
  or or_1 (Output0, and_1_out, and_2_out);
  or or_2 (Output1, and_3_out, and_4_out);
endmodule
